// Logisim project SPM.circ as structural Verilog: 1 circuit, main circuit main
module main (
  input  in_1,
  input  in_2,
  input  A_3,
  input  A_2,
  input  A_1,
  input  A_0,
  input  in_7,
  input  RST
);

  wire adder_1_cout, adder_1_out, adder_2_cout, adder_2_out, adder_3_cout, adder_3_out, and_1_out, and_2_out,
       and_3_out, and_4_out, and_5_out, and_6_out, and_7_out, and_8_out, and_9_out, and_10_out, and_11_out,
       and_12_out, B_out, B_q0, CLK_out, d_ff_1_q, d_ff_2_q, d_ff_3_q, d_ff_4_q, d_ff_5_q, d_ff_6_q,
       d_ff_7_q, d_ff_8_q, d_ff_8_qn, d_ff_9_q, multiplexer_1_out, multiplexer_2_out, multiplexer_3_out,
       not_1_out, not_2_out, not_3_out, not_4_out, or_1_out, t_ff_1_q, t_ff_2_q, t_ff_3_q, t_ff_4_q,
       t_ff_5_q, t_ff_6_q, t_ff_7_q, xor_1_out, xor_2_out, xor_3_out, xor_4_out, xor_5_out, xor_6_out,
       xor_7_out, xor_8_out;

  Multiplexer multiplexer_1 (.in0(in_1), .in1(in_2), .out(multiplexer_1_out), .sel(B_q0));  // open: en
  Clock CLK (.out(CLK_out));
  Multiplexer multiplexer_2 (
    .in0(multiplexer_1_out), .in1(in_7), .out(multiplexer_2_out), .sel(not_2_out));  // open: en
  Shift_Register #(.length(4)) B (
    .in(multiplexer_2_out), .clk(CLK_out), .out(B_out), .clr(RST), .q0(B_q0));  // open: shift, load, d0, d1, q1, d2, q2, d3, q3
  not not_1 (not_1_out, RST);
  and and_1 (and_1_out, B_out, A_3);
  T_Flip_Flop t_ff_1 (.clk(CLK_out), .T(not_1_out), .Q(t_ff_1_q), .reset(RST), .en(not_2_out));  // open: Qn, preset
  xor xor_1 (xor_1_out, B_q0, A_3);
  or or_1 (or_1_out, and_1_out, d_ff_2_q);
  and and_2 (and_2_out, t_ff_1_q, t_ff_2_q);
  T_Flip_Flop t_ff_2 (.clk(CLK_out), .T(t_ff_1_q), .Q(t_ff_2_q), .reset(RST), .en(not_2_out));  // open: Qn, preset
  D_Flip_Flop #(.trigger("high")) d_ff_1 (
    .clk(CLK_out), .D(xor_1_out), .Q(d_ff_1_q), .reset(t_ff_3_q));  // open: Qn, preset, en
  xor xor_2 (xor_2_out, and_1_out, d_ff_2_q);
  D_Flip_Flop #(.trigger("high")) d_ff_2 (
    .clk(CLK_out), .D(or_1_out), .Q(d_ff_2_q), .reset(RST));  // open: Qn, preset, en
  T_Flip_Flop t_ff_3 (.clk(CLK_out), .T(and_2_out), .Q(t_ff_3_q), .reset(RST), .en(not_2_out));  // open: Qn, preset
  D_Flip_Flop #(.trigger("high")) d_ff_3 (
    .clk(CLK_out), .D(xor_2_out), .Q(d_ff_3_q), .reset(RST));  // open: Qn, preset, en
  LED led_1 (.in(t_ff_3_q));
  not not_2 (not_2_out, t_ff_3_q);
  and and_3 (and_3_out, B_out, A_2);
  and and_4 (and_4_out, adder_1_out, and_3_out);
  xor xor_3 (xor_3_out, and_3_out, adder_1_out);
  Adder #(.width(1)) adder_1 (.a(d_ff_3_q), .b(d_ff_4_q), .out(adder_1_out), .cout(adder_1_cout));  // open: cin
  xor xor_4 (xor_4_out, and_4_out, adder_1_cout);
  D_Flip_Flop d_ff_4 (.clk(CLK_out), .D(xor_4_out), .Q(d_ff_4_q), .reset(RST));  // open: Qn, preset, en
  D_Flip_Flop d_ff_5 (.clk(CLK_out), .D(xor_3_out), .Q(d_ff_5_q), .reset(RST));  // open: Qn, preset, en
  and and_5 (and_5_out, B_out, A_1);
  and and_6 (and_6_out, adder_2_out, and_5_out);
  xor xor_5 (xor_5_out, and_5_out, adder_2_out);
  Adder #(.width(1)) adder_2 (.a(d_ff_5_q), .b(d_ff_6_q), .out(adder_2_out), .cout(adder_2_cout));  // open: cin
  xor xor_6 (xor_6_out, and_6_out, adder_2_cout);
  D_Flip_Flop d_ff_6 (.clk(CLK_out), .D(xor_6_out), .Q(d_ff_6_q), .reset(RST));  // open: Qn, preset, en
  and and_7 (and_7_out, B_out, A_0);
  D_Flip_Flop d_ff_7 (.clk(CLK_out), .D(xor_5_out), .Q(d_ff_7_q), .reset(RST));  // open: Qn, preset, en
  and and_8 (and_8_out, adder_3_out, and_7_out);
  xor xor_7 (xor_7_out, and_7_out, adder_3_out);
  Adder #(.width(1)) adder_3 (.a(d_ff_7_q), .b(d_ff_9_q), .out(adder_3_out), .cout(adder_3_cout));  // open: cin
  xor xor_8 (xor_8_out, and_8_out, adder_3_cout);
  and and_9 (and_9_out, t_ff_3_q, ~RST);  // AND_Gate
  Multiplexer multiplexer_3 (.in0(d_ff_8_q), .in1(d_ff_8_qn), .out(multiplexer_3_out), .sel(d_ff_1_q));  // open: en
  D_Flip_Flop d_ff_8 (.clk(CLK_out), .D(xor_7_out), .Q(d_ff_8_q), .Qn(d_ff_8_qn), .reset(RST));  // open: preset, en
  D_Flip_Flop d_ff_9 (.clk(CLK_out), .D(xor_8_out), .Q(d_ff_9_q), .reset(RST));  // open: Qn, preset, en
  T_Flip_Flop t_ff_4 (.clk(CLK_out), .T(and_9_out), .Q(t_ff_4_q), .reset(RST), .en(not_4_out));  // open: Qn, preset
  LED led_2 (.in(not_3_out));
  not not_3 (not_3_out, not_4_out);
  and and_10 (and_10_out, t_ff_4_q, t_ff_5_q);
  T_Flip_Flop t_ff_5 (.clk(CLK_out), .T(t_ff_4_q), .Q(t_ff_5_q), .reset(RST), .en(not_4_out));  // open: Qn, preset
  Shift_Register shift_register_1 (
    .shift(not_4_out), .in(multiplexer_3_out), .clk(CLK_out), .clr(RST));  // open: out, load, d0, q0, d1, q1, d2, q2, d3, q3, d4, q4, d5, q5, d6, q6, d7, q7
  T_Flip_Flop t_ff_6 (.clk(CLK_out), .T(and_10_out), .Q(t_ff_6_q), .reset(RST), .en(not_4_out));  // open: Qn, preset
  and and_11 (and_11_out, and_10_out, t_ff_6_q);
  T_Flip_Flop t_ff_7 (.clk(CLK_out), .T(and_11_out), .Q(t_ff_7_q), .reset(RST), .en(not_4_out));  // open: Qn, preset
  and and_12 (and_12_out, t_ff_7_q, t_ff_4_q);
  not not_4 (not_4_out, and_12_out);
endmodule
